# Fritzing sketch Eye_wiring 2 (saved by Fritzing 0.9.9b)
breadboards: 1

parts:
  Mod1 = Raspberry Pi 4B
  Part3 = 1.2 Inch 8x8 LED Matrix Backpack [part_number=1049]
  Part5 = 1.2 Inch 8x8 LED Matrix Backpack [part_number=1049]

nets:
  VDD: Mod1.3V3, Part3.VDD, Part5.VDD
  N1: Mod1.GPIO2, Part3.SDA, Part5.SDA
  N2: Mod1.GPIO3, Part3.SCL, Part5.SCL
  GND: Mod1.GND, Part3.GND, Part5.GND

custom parts:
  1.2 Inch 8x8 LED Matrix Backpack: This 1.2" 8x8 monochrome LED matrix includes a driver chip for simple control via an I2C interface. The backpack features address-selection jumpers so you can connect up to eight matrices on a single I2C bus.
